# Fritzing sketch AMG8833 (saved by Fritzing 0.9.3b)

parts:
  Raspberry_Pi_1 = Raspberry Pi 3 [part_number=RPI-3-V1.2]
  パーツ1 = Adafruit AMG8833 8x8 GRID EYE

nets:
  3V3: Raspberry_Pi_1.3v3, パーツ1.3.3V
  N1: Raspberry_Pi_1.GPIO2, パーツ1.SDA
  N2: Raspberry_Pi_1.GPIO3, パーツ1.SCL
  GND: Raspberry_Pi_1.GND, パーツ1.GND
